# Fritzing sketch Arduino_Pro_3_3V_Trigger_V4 (saved by Fritzing 0.9.0b)
circuit board: 3.97341cm x 2.55892cm
breadboards: 1

parts:
  R5 = Resistor [tolerance=±5% resistance=50 package=THT]
  GND = female pin header, 10 pins [form="♀ (female)"]
  OSC = Resonator [package=resonator-smd]
  VCC = female pin header, 2 pins [form="♀ (female)"]
  OPTO = IC, DIP package, 8 pins [chip_label=LTV-826]
  Button = female pin header, 2 pins [form="♀ (female)"]
  Encoder = female pin header, 3 pins [form="♀ (female)"]
  GND/FIN = female pin header, 2 pins [form="♀ (female)"]
  ISP = FTDI_BASIC [package=ftdi_basic]
  MEGA = ATmega328 [package=tqfp]
  C1 = Electrolytic Capacitor [capacitance=10µF package="100 mil [THT, electrolytic]"]
  C2 = Electrolytic Capacitor [capacitance=10µF package="100 mil [THT, electrolytic]"]
  R6 = Resistor [tolerance=±5% resistance=50 package=THT]
  R3 = Resistor [tolerance=±5% resistance=10k package=THT]
  C6 = Ceramic Capacitor [capacitance=0.1µF package="200 mil [THT, multilayer]"]
  C4 = Ceramic Capacitor [capacitance=0.1µF package="200 mil [THT, multilayer]"]
  A2 = female pin header, 4 pins [form="♀ (female)"]
  LDO = Voltage Regulator - Variable [package="TO220 [THT]"]
  A1 = female pin header, 2 pins [form="♀ (female)"]
  F_GND = female pin header, 3 pins [form="♀ (female)"]
  GND/SIN = female pin header, 2 pins [form="♀ (female)"]
  LDO_2 = Voltage Regulator LDO [package=sot23-5]

nets:
  GND: R5.Pin_0, GND.pin10, OSC.2, VCC.pin2, Button.pin2, Encoder.pin2, GND/FIN.pin1, ISP.1, ISP.2, MEGA.GND, MEGA.AGND, C1.-, C2.-, R6.Pin_0, C6.1, LDO.ADJ, GND/SIN.pin2, LDO_2.GND
  N1: R5.Pin_1, OPTO.pin2
  N2: GND.pin2, MEGA.PB4(MISO)_D12
  N3: GND.pin3, MEGA.PB3(MOSI_OC2)_D11
  N4: GND.pin4, MEGA.PB5(SCK)_D13
  N5: GND.pin5, MEGA.PB0(ICP)_D8
  N6: GND.pin6, MEGA.PB1(OC1A)_D9
  N7: GND.pin7, MEGA.PB2(SS_OC1B)_D10
  N8: GND.pin8, MEGA.PD4(XCK_T0)_D4
  3.3V: GND.pin9, ISP.3, MEGA.VCC, MEGA.AVCC, C2.+, R3.Pin_1, LDO.OUT, LDO_2.OUT
  N9: OSC.1, MEGA.PB6(XTAL1_TOSC1)
  N10: OSC.3, MEGA.PB7(XTAL2_TOSC2)
  5V: VCC.pin1, C1.+, LDO.IN, LDO_2.IN, LDO_2.EN
  N11: OPTO.pin1, MEGA.ADC6_A0
  N12: OPTO.pin3, MEGA.ADC7_A7
  N13: OPTO.pin4, R6.Pin_1
  N14: OPTO.pin5, OPTO.pin7, F_GND.pin2
  N15: OPTO.pin6, F_GND.pin3
  N16: OPTO.pin8, F_GND.pin1
  N17: Button.pin1, MEGA.PD3(INT1)_D3
  N18: Encoder.pin1, MEGA.PD2(INT0)_D2
  N19: Encoder.pin3, MEGA.PD5(T1)_D5
  N20: GND/FIN.pin2, MEGA.PD6(AIN0)_D6
  N21: ISP.5, MEGA.PD1(TXD)_D1
  N22: ISP.6, C4.1
  N23: ISP.4, MEGA.PD0(RXD)_D0
  N24: MEGA.PD7(AIN1)_D7, GND/SIN.pin1
  N25: MEGA.AREF, C6.0
  N26: MEGA.PC0(ADC0)_A0, A1.pin2
  N27: MEGA.PC1(ADC1)_A1, A1.pin1
  N28: MEGA.PC2(ADC2)_A2, A2.pin1
  N29: MEGA.PC3(ADC3)_A3, A2.pin2
  N30: MEGA.PC4(ADC4_SDA)_A4, A2.pin3
  N31: MEGA.PC5(ADC5_SCL)_A5, A2.pin4
  N32: MEGA.PC6(_RESET), R3.Pin_0, C4.0

notes:
  -
  GND
  S
  A
  B
  IN
  GND/FIN
  GND/SIN
  A0
  A5
  A3
  A4
  DTR
  VCC
  SC
  OC
  R
  DC
  SCK
  SO
  CD
  https://github.com/holymoly/triggster
